# Fritzing sketch Shema_mbed_WiFi_modul (saved by Fritzing 0.9.2b)
breadboards: 1

parts:
  FRDM1 = Freescale FRDM KL25Z
  Part1 = WiFi module 8266 [package=2x5-raf]
  Part2 = USB konvertor

nets:
  GND: FRDM1.GND, Part1.2, Part2.GND
  N1: FRDM1.PTE1, Part1.1
  N2: FRDM1.PTE0, Part1.8
  N3: Part1.3, Part1.5, Part1.7, Part2.VCC

custom parts:
  Freescale FRDM KL25Z: Freescale FRDM razvojni sistem
  USB konvertor: USB kabl sa 3.3V regulatorom
