# Fritzing sketch shema_RGB_LED (saved by Fritzing 0.9.2b)
breadboards: 1

parts:
  Raspberry_Pi1 = Raspberry Pi 2
  LED1 = RGB LED - (4 legs) [package="5 mm [THT]"]
  R1 = Resistor [tolerance=±5% resistance=220 package="1206 [SMD]"]
  R2 = Resistor [tolerance=±5% resistance=220 package="1206 [SMD]"]
  R3 = Resistor [tolerance=±5% resistance=220 package="1206 [SMD]"]

nets:
  N1: Raspberry_Pi1.3v3, LED1.common_anode
  N2: Raspberry_Pi1.GPIO2, R1.Pin_1
  N3: Raspberry_Pi1.GPIO3, R2.Pin_1
  N4: Raspberry_Pi1.GPIO4, R3.Pin_1
  N5: LED1.red_cathode, R1.Pin_0
  N6: LED1.green_cathode, R2.Pin_0
  N7: LED1.blue_cathode, R3.Pin_0
